# Fritzing sketch bread (saved by Fritzing 0.9.3b)
breadboards: 1

parts:
  Raspberry_Pi_1 = Raspberry Pi 3 [part_number=RPI-3-V1.2]
  LED1 = LED - 5mm [color="Red (633nm)" package="5 mm [THT]"]
  LED2 = LED - 5mm [color="Red (633nm)" package="5 mm [THT]"]
  LED3 = LED - 5mm [color="Red (633nm)" package="5 mm [THT]"]
  R1 = Resistor [tolerance=±5% resistance=220 package=THT]
  R2 = Resistor [tolerance=±5% resistance=220 package=THT]
  R3 = Resistor [tolerance=±5% resistance=220 package=THT]
  S4 = Pushbutton [package="[THT]"]
  S5 = Pushbutton [package="[THT]"]
  S6 = Pushbutton [package="[THT]"]
  Part1 = BME280 Breakout

nets (from the schematic view):
  3V3: Raspberry_Pi_1.3v3, Part1.3.3V
  N1: Raspberry_Pi_1.GPIO2, Part1.SDI/SDA
  N2: Raspberry_Pi_1.GPIO3, Part1.SCK/SCL
  GND: Raspberry_Pi_1.GND, R1.Pin_1, R2.Pin_0, R3.Pin_0, S4.Pin_1, S4.Pin_2, S6.Pin_1, S6.Pin_2, Part1.GND
  N3: Raspberry_Pi_1.GPIO13, LED1.cathode
  N4: Raspberry_Pi_1.GPIO19, LED2.cathode
  N5: Raspberry_Pi_1.GPIO26, LED3.cathode
  N6: Raspberry_Pi_1.GPIO21, S6.Pin_3, S6.Pin_4
  N7: Raspberry_Pi_1.GPIO20, S5.Pin_3, S5.Pin_4
  N8: Raspberry_Pi_1.GPIO16, S4.Pin_3, S4.Pin_4
  N9: LED1.anode, R1.Pin_0
  N10: LED2.anode, R2.Pin_1
  N11: LED3.anode, R3.Pin_1
  N12: S5.Pin_1, S5.Pin_2

// code stored in the sketch: bread.ino
import smbus2
import bme280
import time
import RPi.GPIO as GPIO
import random
import math
GPIO.setmode(GPIO.BCM)
GPIO.setwarnings(False)


print("Sviecinats saja profesionalaja skripta, kas tev palidzes izmantot BMW280")
intro()
def intro():
    try:
        kv = int(input("""
    Izvelies darbibu:
    1 - Paspeleties ar pogam
    2 - Aprekinat gazes masu telpa/trauka + gazes atrumu
    Darbiba: """))


        if (kv == 1):
            sensinfo()


        if (kv == 2):
            kalk()


        if (kv < 1) or (kv > 2):
            print("Izvelies 1 vai 2")
            intro()


    except(ValueError):
        print("Nesaportu atbildi, megini velreiz!")
        intro()
    else:
        print("Nesaprotu atbildi, megini velreiz!")
        intro()


def sensinfo():
    port = 1
    address = 0x76
    bus = smbus2.SMBus(port)
    calibration_params = bme280.load_calibration_params(bus, address)
    data = bme280.sample(bus, address, calibration_params)
    GPIO.setup(13,GPIO.OUT) #lilla
    GPIO.setup(19,GPIO.OUT) #Balts
    GPIO.setup(26,GPIO.OUT) #Peleks
    p1 = 16
    p2 = 20
    p3 = 21
    GPIO.setup(p1, GPIO.IN, GPIO.PUD_UP)
    GPIO.setup(p2, GPIO.IN, GPIO.PUD_UP)
    GPIO.setup(p3, GPIO.IN, GPIO.PUD_UP)
    try:
        while True:
            if GPIO.input(16) == GPIO.LOW:
                GPIO.output(13,GPIO.HIGH)
                print("Iegutos datus saglabaju.")
                print(data.temperature)
                print(data.pressure)
                print(data.id)
                print(data.timestamp)
                id1 = data.id
                id2 = data.timestamp
                id3 = data.temperature
                id4 = data.pressure
                time.sleep(1)
                GPIO.output(13,GPIO.LOW)
                
            if GPIO.input(20) == GPIO.LOW:
                GPIO.output(19,GPIO.HIGH)
                print("Iegutos datus neglabaju")
                print(data.temperature)
                print(data.pressure)
                print(data.id)
                print(data.timestamp)
                time.sleep(1)
                GPIO.output(19,GPIO.LOW)


            if GPIO.input(21) == GPIO.LOW:
                GPIO.output(26,GPIO.HIGH)
                print("Saglabatie dati")
                print(id1)
                print(id2)
                print(id3)
                print(id4)
                time.sleep(1)
                GPIO.output(26,GPIO.LOW)             


            else:
                GPIO.output(13,GPIO.LOW)
                GPIO.output(19,GPIO.LOW)
                GPIO.output(26,GPIO.LOW)


    except KeyboardInterrupt:
        print('/n')
        GPIO.cleanup()
    finally:
        GPIO.cleanup()


def kalk():
    port = 1
    address = 0x76
    bus = smbus2.SMBus(port)
    calibration_params = bme280.load_calibration_params(bus, address)
    data = bme280.sample(bus, address, calibration_params)
    R = 8.31
    try:
        while True:
            kv1 = int(input("""
Izvelies gazi:
1 - Gaiss
2 - Oglekla dioksids (Olgskaba gaze)
3 - Viss custom
Darbiba: """))


            if (kv1 == 1):
                Vol1 = float(input("Ievadi telpas/trauka tilpumu kubikmetros: "))
                Mol1 = 28.97
                mass1 = (Mol1 * data.pressure * Vol1) / (R * (data.temperature + 273))
                print("Gazes masa telpa = ", mass1, " kg.")
                vv21 = math.sqrt(3 * R * (data.temperature + 273) / Mol1)
                print("Gazes atrums telpa ir", vv21, " m/s")
                kalk()


            if (kv1 == 2):
                Vol2 = float(input("Ievadi telpas/trauka tilpumu kubikmetros: "))
                Mol2 = 44.01
                mass2 = (Mol2 * data.pressure * Vol2) / (R * (data.temperature + 273))
                print("Gazes masa telpa = ", mass2, " kg.")
                vv222 = math.sqrt(3 * R * (data.temperature + 273) / Mol2)
                print("Gazes atrums telpa ir", vv222, " m/s" )
                kalk()


            if (kv1 == 3):
                Vol3 = float(input("Ievadi telpas/trauka tilpumu kubikmetros: "))
                Mol3 = float(input("Ievadi gazes molmasu g/mol = "))
                mass3 = (Mol3 * data.pressure *Vol3) / (R * (data.temperature + 273))
                print("Gazes masa telpa = ", mass3, " kg.")
                vv333 = math.sqrt(3 * R * (data.temperature + 273) / Mol3)
                print("Gazes atrums telpa ir", vv333, " m/s" )
                kalk()


            if (kv1 < 1) or (kv1 > 3):
                print("Izvelies 1 vai 2 vai 3")
                kalk()
    
    except(ValueError):
        print("Nesaportu atbildi, megini velreiz!")
        kalk()
    else:
        print("Nesaprotu atbildi, megini velreiz!")
        kalk()
